# Fritzing sketch Calibracion_AC712 (saved by Fritzing 0.9.9b)

parts:
  Componente1 = Arduino Uno (Rev3)
  Componente2 = ACS712 Low Current Sensor Board v12
  R1 = Resistor [tolerance=±5% resistance=12 power=5W package="0402 [SMD]"]
  R2 = Resistor [tolerance=±5% resistance=12 power=5W package="0402 [SMD]"]
  R3 = Resistor [tolerance=±5% resistance=12 power=5W package="0402 [SMD]"]
  R4 = Resistor [tolerance=±5% resistance=12 power=5W package="0402 [SMD]"]
  R5 = Resistor [tolerance=±5% resistance=12 power=5W package="0402 [SMD]"]
  R6 = Resistor [tolerance=±5% resistance=12 power=5W package="0402 [SMD]"]
  R7 = Resistor [tolerance=±5% resistance=12 power=5W package="0402 [SMD]"]
  R8 = Resistor [tolerance=±5% resistance=12 power=5W package="0402 [SMD]"]
  U1 = SWITCH-SPST-2 [package=switch-spst-vertical]
  U2 = SWITCH-SPST-2 [package=switch-spst-vertical]
  U3 = SWITCH-SPST-2 [package=switch-spst-vertical]
  U4 = SWITCH-SPST-2 [package=switch-spst-vertical]
  U5 = Transformer [package=transformer]
  F1 = FUSE [package=fuse_5mm]
  V1 = AC Power [voltage=5 frequency=60]

nets:
  N1: Componente1.A0, Componente2.VO
  5V: Componente1.5V, Componente2.5V
  GND: Componente1.GND, Componente2.GND
  N2: Componente2.IP+, F1.2
  N3: Componente2.IP-, U1.O, U2.O, U3.O, U4.O
  N4: R1.Pin_0, U1.P
  N5: R1.Pin_1, R2.Pin_0
  N6: R2.Pin_1, R4.Pin_1, R6.Pin_1, R8.Pin_1, U5.3
  N7: R3.Pin_0, U2.P
  N8: R3.Pin_1, R4.Pin_0
  N9: R5.Pin_0, U3.P
  N10: R5.Pin_1, R6.Pin_0
  N11: R7.Pin_0, U4.P
  N12: R7.Pin_1, R8.Pin_0
  N13: U5.1, V1.V+
  N14: U5.2, V1.V-
  N15: U5.4, F1.1
